// Logisim project control unit revised.circ as structural Verilog: 1 circuit, main circuit control unit
module control_unit (
  input  clk,
  input  [31:0] inst_in,
  input  [31:0] alu_out,
  input  z_in,
  input  c_in,
  output [2:0] ALU_Op,
  output ALU_Src1,
  output [1:0] ALU_Src2,
  output PC_Src,
  output [4:0] rs2,
  output Sub,
  output [4:0] rd,
  output I_Or_D,
  output Mem2Reg,
  output Mem_Read,
  output Reg_Write,
  output IR_Load,
  output Reg_Src_2,
  output [31:0] imm,
  output PC_Load,
  output ALU_Out_Ld,
  output mdr_load,
  output A_Load,
  output Mem_Write,
  output B_Load,
  output [4:0] rs1,
  output [1:0] Width,
  output extend,
  output halt
);

  wire and_1_out, and_2_out, and_3_out, and_4_out, and_5_out, and_6_out, and_7_out, and_11_out, and_12_out,
       and_13_out, and_14_out, and_15_out, and_16_out, and_17_out, and_18_out, and_20_out, and_21_out,
       and_26_out, and_33_out, and_34_out, and_35_out, and_38_out, and_39_out, and_40_out, AUIPC, BRANCH,
       branch_z, custom_ALU_Op, Decode, decoder_1_out0, decoder_1_out1, decoder_1_out2, decoder_1_out3,
       decoder_1_out4, decoder_2_out0, decoder_2_out1, decoder_2_out4, decoder_2_out5, decoder_2_out6,
       decoder_2_out7, decoder_3_out0, decoder_3_out4, decoder_3_out6, decoder_4_out0, decoder_4_out1,
       decoder_4_out3, decoder_5_out0, decoder_5_out1, decoder_5_out3, decoder_5_out4, decoder_5_out5,
       I_Type, JAL, JALR, LOAD, LUI, MISC_MEM, multiplexer_3_out, multiplexer_11_out, multiplexer_18_out,
       nor_1_out, not_2_out, OP, OP_IMM, or_1_out, or_2_out, or_3_out, or_4_out, or_6_out, or_7_out,
       or_10_out, STORE, SYSTEM, tty_write, U_Type, valid_opc, xnor_2_out;
  wire [1:0] multiplexer_2_out, multiplexer_4_out, multiplexer_6_out, multiplexer_7_out, multiplexer_8_out,
       multiplexer_10_out, multiplexer_12_out, multiplexer_14_out, multiplexer_15_out, multiplexer_16_out,
       multiplexer_19_out, not_1_out, not_3_out;
  wire [2:0] and_8_out, and_9_out, and_10_out, bit_extender_1_out, bit_extender_2_out, bit_extender_3_out,
       branch_type, counter_1_q, custom_bus_ALU_Op, multiplexer_5_out, multiplexer_17_out,
       multiplexer_20_out, xnor_1_out;
  wire [4:0] multiplexer_9_out;
  wire [6:0] multiplexer_13_out, tty_input;
  wire [19:0] and_41_out, and_42_out, and_43_out, and_44_out, and_45_out, bit_extender_4_out,
       bit_extender_5_out, bit_extender_6_out, bit_extender_7_out, bit_extender_8_out, imm_i, imm_s, imm_sb,
       or_12_out, or_13_out;
  wire [30:0] bit_extender_9_out;
  wire [31:0] bit_extender_10_out;

  Multiplexer #(.width(3), .enable("false")) multiplexer_1 (
    .in0(inst_in[14:12]), .in1(custom_bus_ALU_Op), .sel(custom_ALU_Op));  // open: out
  Pull_Resistor pull_resistor_1 (.node(custom_ALU_Op));
  Decoder #(.select(3)) decoder_1 (
    .out0(decoder_1_out0), .out1(decoder_1_out1), .out2(decoder_1_out2), .out3(decoder_1_out3),
    .out4(decoder_1_out4), .sel(counter_1_q));  // open: out5, out6, out7, en
  Counter #(.width(3), .max('h4), .trigger("falling")) counter_1 (
    .Q(counter_1_q), .clk(clk));  // open: load, D, count, carry, clr
  buf buffer_1 (Decode, decoder_1_out1);
  and and_1 (and_1_out, decoder_1_out3, SYSTEM);
  and and_2 (and_2_out, decoder_1_out4, or_1_out);
  buf buffer_2 (Mem_Read, decoder_1_out0);
  buf buffer_3 (B_Load, decoder_1_out1);
  buf buffer_4 (A_Load, decoder_1_out1);
  and and_3 (and_3_out, decoder_1_out2, OP);
  buf buffer_5 (ALU_Out_Ld, and_3_out);
  buf buffer_6 (ALU_Src1, and_3_out);
  Multiplexer #(.width(2), .enable("false")) multiplexer_2 (
    .in1(2'b10), .out(multiplexer_2_out), .sel(and_3_out));  // open: in0
  assign ALU_Src2 = multiplexer_2_out;  // Buffer buffer_7, 2 bits wide
  Multiplexer #(.enable("false")) multiplexer_3 (
    .in1(inst_in[30]), .out(multiplexer_3_out), .sel(and_3_out));  // open: in0
  buf buffer_8 (Sub, multiplexer_3_out);
  buf buffer_9 (ALU_Out_Ld, and_1_out);
  buf buffer_10 (ALU_Src1, and_1_out);
  Multiplexer #(.width(2), .enable("false")) multiplexer_4 (
    .in1(2'b01), .out(multiplexer_4_out), .sel(and_1_out));  // open: in0
  assign ALU_Src2 = multiplexer_4_out;  // Buffer buffer_11, 2 bits wide
  or or_1 (or_1_out, JAL, JALR);
  buf buffer_12 (PC_Load, and_2_out);
  buf buffer_13 (PC_Src, and_2_out);
  Pull_Resistor pull_resistor_2 (.node(Sub));
  Pull_Resistor pull_resistor_3 (.node(I_Or_D));
  Pull_Resistor pull_resistor_4 (.node(Mem_Read));
  Pull_Resistor pull_resistor_5 (.node(IR_Load));
  Pull_Resistor pull_resistor_6 (.node(ALU_Out_Ld));
  Pull_Resistor pull_resistor_7 (.node(A_Load));
  Pull_Resistor pull_resistor_8 (.node(B_Load));
  Pull_Resistor pull_resistor_9 (.node(inst_in[19:15]));
  Decoder #(.select(3), .enable("false")) decoder_2 (
    .out0(decoder_2_out0), .out1(decoder_2_out1), .out4(decoder_2_out4), .out5(decoder_2_out5),
    .out6(decoder_2_out6), .out7(decoder_2_out7), .sel(inst_in[14:12]));  // open: out2, out3
  Decoder #(.select(3), .enable("false")) decoder_3 (
    .out0(decoder_3_out0), .out4(decoder_3_out4), .out6(decoder_3_out6), .sel(inst_in[14:12]));  // open: out1, out2, out3, out5, out7
  Multiplexer #(.width(3), .enable("false")) multiplexer_5 (
    .in1(inst_in[14:12]), .out(multiplexer_5_out), .sel(and_3_out));  // open: in0
  assign ALU_Op = multiplexer_5_out;  // Buffer buffer_14, 3 bits wide
  and and_4 (and_4_out, decoder_1_out3, JAL);
  buf buffer_15 (ALU_Out_Ld, and_4_out);
  Multiplexer #(.width(2), .enable("false")) multiplexer_6 (
    .in1(2'b10), .out(multiplexer_6_out), .sel(and_4_out));  // open: in0
  assign ALU_Src2 = multiplexer_6_out;  // Buffer buffer_16, 2 bits wide
  and and_5 (and_5_out, decoder_1_out4, or_7_out);
  Pull_Resistor pull_resistor_10 (.node(ALU_Src1));
  or or_2 (or_2_out, decoder_2_out0, decoder_2_out1);
  or or_3 (or_3_out, decoder_2_out4, decoder_2_out5);
  or or_4 (or_4_out, decoder_2_out6, decoder_2_out7);
  or or_5 (branch_z, decoder_3_out0, decoder_3_out4, decoder_3_out6);
  buf buffer_17 (IR_Load, decoder_1_out0);
  or or_6 (or_6_out, JAL, JALR, BRANCH);
  and and_6 (and_6_out, decoder_1_out1, or_6_out);
  buf buffer_18 (ALU_Out_Ld, and_6_out);
  and and_7 (and_7_out, decoder_1_out2, JAL);
  buf buffer_19 (Reg_Write, and_7_out);
  or or_7 (or_7_out, U_Type, OP, OP_IMM);
  buf buffer_20 (Reg_Write, and_5_out);
  Pull_Resistor pull_resistor_11 (.node(ALU_Op));
  Pull_Resistor pull_resistor_12 (.node(ALU_Src2));
  Pull_Resistor pull_resistor_13 (.node(PC_Src));
  assign bit_extender_1_out = {{2{or_2_out}}, or_2_out};  // Bit_Extender bit_extender_1
  assign and_8_out = bit_extender_1_out & 3'b100;  // AND_Gate and_8, 3 bits wide
  assign bit_extender_2_out = {{2{or_3_out}}, or_3_out};  // Bit_Extender bit_extender_2
  assign and_9_out = bit_extender_2_out & 3'b010;  // AND_Gate and_9, 3 bits wide
  assign bit_extender_3_out = {{2{or_4_out}}, or_4_out};  // Bit_Extender bit_extender_3
  assign and_10_out = bit_extender_3_out & 3'b011;  // AND_Gate and_10, 3 bits wide
  and and_11 (and_11_out, decoder_1_out3, JALR);
  buf buffer_21 (ALU_Out_Ld, and_11_out);
  buf buffer_22 (ALU_Src1, and_11_out);
  Multiplexer #(.width(2), .enable("false")) multiplexer_7 (
    .in1(2'b10), .out(multiplexer_7_out), .sel(and_11_out));  // open: in0
  assign ALU_Src2 = multiplexer_7_out;  // Buffer buffer_23, 2 bits wide
  assign branch_type = and_8_out | and_9_out | and_10_out;  // OR_Gate or_8, 3 bits wide
  and and_12 (and_12_out, decoder_1_out1, BRANCH);
  Multiplexer #(.width(2), .enable("false")) multiplexer_8 (
    .in1(2'b10), .out(multiplexer_8_out), .sel(and_12_out));  // open: in0
  assign ALU_Src2 = multiplexer_8_out;  // Buffer buffer_24, 2 bits wide
  and and_13 (and_13_out, decoder_1_out3, LOAD);
  and and_14 (and_14_out, decoder_1_out4, LOAD);
  buf buffer_25 (Mem2Reg, and_14_out);
  buf buffer_26 (Reg_Write, and_14_out);
  Pull_Resistor pull_resistor_14 (.node(Mem2Reg));
  Pull_Resistor pull_resistor_15 (.node(Reg_Write));
  Pull_Resistor pull_resistor_16 (.node(Reg_Src_2));
  Pull_Resistor pull_resistor_17 (.node(PC_Load));
  Pull_Resistor pull_resistor_18 (.node(mdr_load));
  Pull_Resistor pull_resistor_19 (.node(Mem_Write));
  Pull_Resistor pull_resistor_20 (.node(Width));
  Pull_Resistor pull_resistor_21 (.node(extend));
  and and_15 (and_15_out, decoder_1_out1, SYSTEM);
  buf buffer_27 (Mem_Read, and_13_out);
  buf buffer_28 (mdr_load, and_13_out);
  buf buffer_29 (I_Or_D, and_13_out);
  assign not_1_out = ~inst_in[13:12];  // NOT_Gate not_1, 2 bits wide
  Pull_Resistor pull_resistor_22 ();  // open: node
  or or_9 (I_Type, LOAD, JALR, OP_IMM);
  Multiplexer #(.width(5), .enable("false")) multiplexer_9 (
    .in1(5'b01010), .out(multiplexer_9_out), .sel(and_15_out));  // open: in0
  assign inst_in[19:15] = multiplexer_9_out;  // Buffer buffer_30, 5 bits wide
  and and_16 (and_16_out, decoder_1_out2, U_Type);
  buf buffer_31 (ALU_Out_Ld, and_16_out);
  Multiplexer #(.width(2), .enable("false")) multiplexer_10 (
    .in1(2'b10), .out(multiplexer_10_out), .sel(and_16_out));  // open: in0
  assign ALU_Src2 = multiplexer_10_out;  // Buffer buffer_32, 2 bits wide
  buf buffer_33 (extend, multiplexer_11_out);
  Multiplexer #(.enable("false")) multiplexer_11 (
    .in1(not_2_out), .out(multiplexer_11_out), .sel(and_13_out));  // open: in0
  not not_2 (not_2_out, inst_in[14]);
  assign Width = multiplexer_12_out;  // Buffer buffer_34, 2 bits wide
  Multiplexer #(.width(2), .enable("false")) multiplexer_12 (
    .in1(not_1_out), .out(multiplexer_12_out), .sel(and_13_out));  // open: in0
  and and_17 (and_17_out, decoder_1_out4, SYSTEM);
  buf buffer_35 (tty_write, and_17_out);
  assign tty_input = multiplexer_13_out;  // Buffer buffer_36, 7 bits wide
  Multiplexer #(.width(7), .enable("false")) multiplexer_13 (
    .in1(alu_out[6:0]), .out(multiplexer_13_out), .sel(and_17_out));  // open: in0
  Decoder #(.select(2), .disabled(0)) decoder_4 (
    .out0(decoder_4_out0), .out1(decoder_4_out1), .out3(decoder_4_out3), .sel(inst_in[6:5]), .en(valid_opc));  // open: out2
  and and_18 (and_18_out, decoder_1_out3, STORE);
  buf buffer_37 (I_Or_D, and_18_out);
  buf buffer_38 (Mem_Write, and_18_out);
  buf buffer_39 (extend, and_18_out);
  and and_19 (valid_opc, inst_in[0], inst_in[1]);
  or or_10 (or_10_out, LOAD, STORE);
  and and_20 (and_20_out, decoder_1_out2, or_10_out);
  buf buffer_40 (ALU_Out_Ld, and_20_out);
  buf buffer_41 (ALU_Src1, and_20_out);
  Multiplexer #(.width(2), .enable("false")) multiplexer_14 (
    .in1(2'b10), .out(multiplexer_14_out), .sel(and_20_out));  // open: in0
  assign ALU_Src2 = multiplexer_14_out;  // Buffer buffer_42, 2 bits wide
  Multiplexer #(.width(2), .enable("false")) multiplexer_15 (
    .in1(not_3_out), .out(multiplexer_15_out), .sel(and_18_out));  // open: in0
  assign not_3_out = ~inst_in[13:12];  // NOT_Gate not_3, 2 bits wide
  and and_21 (and_21_out, decoder_1_out4, BRANCH);
  buf buffer_43 (PC_Load, and_21_out);
  buf buffer_44 (PC_Src, and_21_out);
  Decoder #(.select(3), .disabled(0)) decoder_5 (
    .out0(decoder_5_out0), .out1(decoder_5_out1), .out3(decoder_5_out3), .out4(decoder_5_out4),
    .out5(decoder_5_out5), .sel(inst_in[4:2]), .en(valid_opc));  // open: out2, out6, out7
  and and_22 (LOAD, decoder_4_out0, decoder_5_out0);
  and and_23 (STORE, decoder_4_out1, decoder_5_out0);
  and and_24 (BRANCH, decoder_4_out3, decoder_5_out0);
  and and_25 (halt, Decode, nor_1_out);
  nor nor_1 (nor_1_out, MISC_MEM, LOAD, OP_IMM, AUIPC, STORE, OP, LUI, BRANCH, JALR, JAL, SYSTEM);
  and and_26 (and_26_out, decoder_1_out3, OP_IMM);
  assign Width = multiplexer_15_out;  // Buffer buffer_45, 2 bits wide
  and and_27 (MISC_MEM, decoder_4_out0, decoder_5_out3);
  and and_28 (OP_IMM, decoder_4_out0, decoder_5_out4);
  and and_29 (LUI, decoder_4_out1, decoder_5_out5);
  and and_30 (OP, decoder_4_out1, decoder_5_out4);
  and and_31 (JAL, decoder_5_out3, decoder_4_out3);
  and and_32 (JALR, decoder_5_out1, decoder_4_out3);
  and and_33 (and_33_out, decoder_1_out2, BRANCH);
  buf buffer_46 (ALU_Out_Ld, and_26_out);
  buf buffer_47 (ALU_Src1, and_26_out);
  Multiplexer #(.width(2), .enable("false")) multiplexer_16 (
    .in1(2'b10), .out(multiplexer_16_out), .sel(and_26_out));  // open: in0
  assign ALU_Src2 = multiplexer_16_out;  // Buffer buffer_48, 2 bits wide
  Multiplexer #(.width(3), .enable("false")) multiplexer_17 (
    .in1(inst_in[14:12]), .out(multiplexer_17_out), .sel(and_26_out));  // open: in0
  assign ALU_Op = multiplexer_17_out;  // Buffer buffer_49, 3 bits wide
  and and_34 (and_34_out, xnor_1_out[0], xnor_1_out[1], xnor_1_out[2]);
  and and_35 (and_35_out, and_26_out, and_34_out);
  Multiplexer #(.enable("false")) multiplexer_18 (
    .in1(inst_in[30]), .out(multiplexer_18_out), .sel(and_35_out));  // open: in0
  buf buffer_50 (Sub, multiplexer_18_out);
  and and_36 (AUIPC, decoder_4_out0, decoder_5_out5);
  and and_37 (SYSTEM, decoder_5_out4, decoder_4_out3);
  buf buffer_51 (PC_Src, and_33_out);
  buf buffer_52 (PC_Load, and_33_out);
  buf buffer_53 (A_Load, and_33_out);
  buf buffer_54 (B_Load, and_33_out);
  assign xnor_1_out = ~(inst_in[14:12] ^ 3'b101);  // XNOR_Gate xnor_1, 3 bits wide
  and and_38 (and_38_out, decoder_1_out2, LUI);
  buf buffer_55 (ALU_Src1, and_38_out);
  and and_39 (and_39_out, decoder_1_out3, BRANCH);
  xnor xnor_2 (xnor_2_out, z_in, branch_z);
  and and_40 (and_40_out, and_39_out, xnor_2_out);
  buf buffer_56 (ALU_Src1, and_39_out);
  buf buffer_57 (Sub, and_39_out);
  buf buffer_58 (PC_Load, and_40_out);
  or or_11 (U_Type, AUIPC, LUI);
  Pull_Resistor pull_resistor_23 (.node(tty_input));
  TTY tty_1 (.data(tty_input), .clk(clk), .we(tty_write));  // open: clr
  Pull_Resistor pull_resistor_24 (.node(tty_write));
  Multiplexer #(.width(2), .enable("false")) multiplexer_19 (
    .in1(2'b01), .out(multiplexer_19_out), .sel(and_39_out));  // open: in0
  assign ALU_Src2 = multiplexer_19_out;  // Buffer buffer_59, 2 bits wide
  assign bit_extender_4_out = {{19{U_Type}}, U_Type};  // Bit_Extender bit_extender_4
  assign bit_extender_5_out = {{19{STORE}}, STORE};  // Bit_Extender bit_extender_5
  assign bit_extender_6_out = {{19{I_Type}}, I_Type};  // Bit_Extender bit_extender_6
  assign bit_extender_7_out = {{19{JAL}}, JAL};  // Bit_Extender bit_extender_7
  assign bit_extender_8_out = {{19{BRANCH}}, BRANCH};  // Bit_Extender bit_extender_8
  Multiplexer #(.width(3), .enable("false")) multiplexer_20 (
    .in1(branch_type), .out(multiplexer_20_out), .sel(and_39_out));  // open: in0
  assign ALU_Op = multiplexer_20_out;  // Buffer buffer_60, 3 bits wide
  assign and_41_out = inst_in[31:12] & bit_extender_4_out;  // AND_Gate and_41, 20 bits wide
  assign and_42_out = imm_s & bit_extender_5_out;  // AND_Gate and_42, 20 bits wide
  assign and_43_out = imm_i & bit_extender_6_out;  // AND_Gate and_43, 20 bits wide
  assign and_44_out = {inst_in[31], inst_in[19:12], inst_in[20], inst_in[30:21]} & bit_extender_7_out;  // AND_Gate and_44, 20 bits wide
  assign and_45_out = imm_sb & bit_extender_8_out;  // AND_Gate and_45, 20 bits wide
  assign or_12_out = and_42_out | and_43_out;  // OR_Gate or_12, 20 bits wide
  assign or_13_out = and_44_out | and_45_out;  // OR_Gate or_13, 20 bits wide
  assign bit_extender_9_out = {{11{or_13_out[19]}}, or_13_out};  // Bit_Extender bit_extender_9
  assign bit_extender_10_out = {{12{or_12_out[19]}}, or_12_out};  // Bit_Extender bit_extender_10
  assign imm = {and_41_out, {12{1'b0}}} | bit_extender_10_out | {bit_extender_9_out, 1'b0};  // OR_Gate or_14, 32 bits wide
  assign imm_i = {{8{inst_in[31]}}, inst_in[31:20]};  // Bit_Extender bit_extender_11
  assign imm_s = {{8{inst_in[31]}}, {inst_in[31:25], inst_in[11:7]}};  // Bit_Extender bit_extender_12
  assign imm_sb = {{8{inst_in[31]}}, {inst_in[31], inst_in[7], inst_in[30:25], inst_in[11:8]}};  // Bit_Extender bit_extender_13

  assign rd = inst_in[11:7];
  assign rs1 = inst_in[19:15];
  assign rs2 = inst_in[24:20];

  // Other names for the same wires on the sheet: inst[31:0] = inst_in; funct7[6:0] = inst_in[31:25];
  //   imm_u[19:0] = inst_in[31:12]; imm_uj[19:0] = {inst_in[31], inst_in[19:12], inst_in[20], inst_in[30:21]};
  //   ALU_Op_Out[2:0] = ALU_Op; c = c_in; funct3[2:0] = inst_in[14:12]; inst_4_2[2:0] = inst_in[4:2];
  //   inst_6_5[1:0] = inst_in[6:5]; Mdr_Ld = mdr_load; sub_out = Sub; z = z_in

  // Notes on the sheet:
  //   buffer_2 drives only 1 and floats otherwise
  //   buffer_3 drives only 1 and floats otherwise
  //   buffer_4 drives only 1 and floats otherwise
  //   buffer_5 drives only 1 and floats otherwise
  //   buffer_6 drives only 1 and floats otherwise
  //   buffer_7 drives only 1 and floats otherwise
  //   buffer_8 drives only 1 and floats otherwise
  //   buffer_9 drives only 1 and floats otherwise
  //   buffer_10 drives only 1 and floats otherwise
  //   buffer_11 drives only 1 and floats otherwise
  //   buffer_12 drives only 1 and floats otherwise
  //   buffer_13 drives only 1 and floats otherwise
  //   buffer_14 drives only 1 and floats otherwise
  //   buffer_15 drives only 1 and floats otherwise
  //   buffer_16 drives only 1 and floats otherwise
  //   buffer_17 drives only 1 and floats otherwise
  //   buffer_18 drives only 1 and floats otherwise
  //   buffer_19 drives only 1 and floats otherwise
  //   buffer_20 drives only 1 and floats otherwise
  //   buffer_21 drives only 1 and floats otherwise
  //   buffer_22 drives only 1 and floats otherwise
  //   buffer_23 drives only 1 and floats otherwise
  //   buffer_24 drives only 1 and floats otherwise
  //   buffer_25 drives only 1 and floats otherwise
  //   buffer_26 drives only 1 and floats otherwise
  //   buffer_27 drives only 1 and floats otherwise
  //   buffer_28 drives only 1 and floats otherwise
  //   buffer_29 drives only 1 and floats otherwise
  //   buffer_30 drives only 1 and floats otherwise
  //   buffer_31 drives only 1 and floats otherwise
  //   buffer_32 drives only 1 and floats otherwise
  //   buffer_33 drives only 1 and floats otherwise
  //   buffer_34 drives only 1 and floats otherwise
  //   buffer_35 drives only 1 and floats otherwise
  //   buffer_36 drives only 1 and floats otherwise
  //   buffer_37 drives only 1 and floats otherwise
  //   buffer_38 drives only 1 and floats otherwise
  //   buffer_39 drives only 1 and floats otherwise
  //   buffer_40 drives only 1 and floats otherwise
  //   buffer_41 drives only 1 and floats otherwise
  //   buffer_42 drives only 1 and floats otherwise
  //   buffer_43 drives only 1 and floats otherwise
  //   buffer_44 drives only 1 and floats otherwise
  //   buffer_45 drives only 1 and floats otherwise
  //   buffer_46 drives only 1 and floats otherwise
  //   buffer_47 drives only 1 and floats otherwise
  //   buffer_48 drives only 1 and floats otherwise
  //   buffer_49 drives only 1 and floats otherwise
  //   buffer_50 drives only 1 and floats otherwise
  //   buffer_51 drives only 1 and floats otherwise
  //   buffer_52 drives only 1 and floats otherwise
  //   buffer_53 drives only 1 and floats otherwise
  //   buffer_54 drives only 1 and floats otherwise
  //   buffer_55 drives only 1 and floats otherwise
  //   buffer_56 drives only 1 and floats otherwise
  //   buffer_57 drives only 1 and floats otherwise
  //   buffer_58 drives only 1 and floats otherwise
  //   buffer_59 drives only 1 and floats otherwise
  //   buffer_60 drives only 1 and floats otherwise
endmodule
